// Logisim project Memory12x8Circuit.circ as structural Verilog: 2 circuits, main circuit main
module main (
);

  Memory12x8 memory12x8_1 ();  // open: address, WR, data
endmodule

module Memory12x8 (
  input  [7:0] address,
  input  WR,
  output [7:0] data
);

  wire decoder_1_out0, decoder_1_out1, decoder_1_out2;

  Decoder #(.select(2)) decoder_1 (
    .out0(decoder_1_out0), .out1(decoder_1_out1), .out2(decoder_1_out2), .out3(WR));  // open: sel, en
  RAM #(.databus("bidir")) ram_1 (.addr(address), .we(WR), .oe(decoder_1_out0), .clk(decoder_1_out0), .data(data));
  RAM #(.databus("bidir")) ram_2 (.addr(address), .we(WR), .oe(decoder_1_out1), .clk(decoder_1_out1), .data(data));
  RAM #(.databus("bidir")) ram_3 (.addr(address), .we(WR), .oe(decoder_1_out2), .clk(decoder_1_out2), .data(data));
  RAM #(.databus("bidir")) ram_4 (.addr(address), .we(WR), .oe(WR), .clk(WR), .data(data));
  RAM #(.databus("bidir")) ram_5 (.addr(address), .we(WR), .oe(decoder_1_out0), .clk(decoder_1_out0), .data(data));
  RAM #(.databus("bidir")) ram_6 (.addr(address), .we(WR), .oe(decoder_1_out1), .clk(decoder_1_out1), .data(data));
  RAM #(.databus("bidir")) ram_7 (.addr(address), .we(WR), .oe(decoder_1_out2), .clk(decoder_1_out2), .data(data));
  RAM #(.databus("bidir")) ram_8 (.addr(address), .we(WR), .oe(WR), .clk(WR), .data(data));
endmodule
