// Logisim project ROM_BIP_TRS.circ as structural Verilog: 1 circuit, main circuit main
module main (
);

  wire decoder_1_out0, decoder_1_out1, decoder_1_out2, decoder_1_out3, decoder_1_out4, decoder_1_out5,
       decoder_1_out6, decoder_1_out7, decoder_1_out8, decoder_1_out9, decoder_1_out10, decoder_1_out11,
       decoder_1_out12, decoder_1_out13, decoder_1_out14, decoder_1_out15, transistor_1_out,
       transistor_7_out, transistor_13_out, transistor_19_out, undriven;

  Decoder #(.select(4)) decoder_1 (
    .out0(decoder_1_out0), .out1(decoder_1_out1), .out2(decoder_1_out2), .out3(decoder_1_out3),
    .out4(decoder_1_out4), .out5(decoder_1_out5), .out6(decoder_1_out6), .out7(decoder_1_out7),
    .out8(decoder_1_out8), .out9(decoder_1_out9), .out10(decoder_1_out10), .out11(decoder_1_out11),
    .out12(decoder_1_out12), .out13(decoder_1_out13), .out14(decoder_1_out14), .out15(decoder_1_out15));  // open: sel, en
  Transistor transistor_1 (.in(decoder_1_out1), .out(transistor_1_out), .gate(undriven));
  Transistor transistor_2 (.in(decoder_1_out2), .out(transistor_1_out), .gate(undriven));
  Transistor transistor_3 (.in(decoder_1_out3), .out(transistor_1_out), .gate(undriven));
  Transistor transistor_4 (.in(decoder_1_out6), .out(transistor_1_out), .gate(undriven));
  Transistor transistor_5 (.in(decoder_1_out7), .out(transistor_1_out), .gate(undriven));
  Transistor transistor_6 (.in(decoder_1_out11), .out(transistor_1_out), .gate(undriven));
  Transistor transistor_7 (.in(decoder_1_out4), .out(transistor_7_out), .gate(undriven));
  Transistor transistor_8 (.in(decoder_1_out8), .out(transistor_7_out), .gate(undriven));
  Transistor transistor_9 (.in(decoder_1_out9), .out(transistor_7_out), .gate(undriven));
  Transistor transistor_10 (.in(decoder_1_out12), .out(transistor_7_out), .gate(undriven));
  Transistor transistor_11 (.in(decoder_1_out13), .out(transistor_7_out), .gate(undriven));
  Transistor transistor_12 (.in(decoder_1_out14), .out(transistor_7_out), .gate(undriven));
  Transistor transistor_13 (.in(decoder_1_out1), .out(transistor_13_out), .gate(undriven));
  Transistor transistor_14 (.in(decoder_1_out2), .out(transistor_13_out), .gate(undriven));
  Transistor transistor_15 (.in(decoder_1_out6), .out(transistor_13_out), .gate(undriven));
  Transistor transistor_16 (.in(decoder_1_out8), .out(transistor_13_out), .gate(undriven));
  Transistor transistor_17 (.in(decoder_1_out12), .out(transistor_13_out), .gate(undriven));
  Transistor transistor_18 (.in(decoder_1_out13), .out(transistor_13_out), .gate(undriven));
  Transistor transistor_19 (.in(decoder_1_out0), .out(transistor_19_out), .gate(undriven));
  Transistor transistor_20 (.in(decoder_1_out2), .out(transistor_19_out), .gate(undriven));
  Transistor transistor_21 (.in(decoder_1_out3), .out(transistor_19_out), .gate(undriven));
  Transistor transistor_22 (.in(decoder_1_out6), .out(transistor_19_out), .gate(undriven));
  Transistor transistor_23 (.in(decoder_1_out9), .out(transistor_19_out), .gate(undriven));
endmodule
