// Logisim project washingmachinetimer.circ as structural Verilog: 1 circuit, main circuit washingmachinetimer
module washingmachinetimer (
  input  in_1,
  output wash,
  output rinse,
  output spin,
  output stop
);

  wire clock_1_out, decoder_1_out0, decoder_1_out1, decoder_1_out2, decoder_1_out3, decoder_1_out4,
       decoder_1_out5, decoder_1_out6, decoder_1_out7, decoder_1_out8, decoder_1_out9, decoder_1_out10,
       decoder_1_out11, decoder_1_out12, decoder_1_out13, decoder_1_out14, decoder_1_out15;
  wire [3:0] counter_1_q;

  Counter #(.max('hf), .width(4)) counter_1 (
    .clr(1'b0), .load(1'b0), .up(1'b1), .count(1'b1), .clk(clock_1_out), .Q(counter_1_q));  // open: D, carry
  Clock clock_1 (.out(clock_1_out));
  Decoder #(.select(4)) decoder_1 (
    .out0(decoder_1_out0), .out1(decoder_1_out1), .out2(decoder_1_out2), .out3(decoder_1_out3),
    .out4(decoder_1_out4), .out5(decoder_1_out5), .out6(decoder_1_out6), .out7(decoder_1_out7),
    .out8(decoder_1_out8), .out9(decoder_1_out9), .out10(decoder_1_out10), .out11(decoder_1_out11),
    .out12(decoder_1_out12), .out13(decoder_1_out13), .out14(decoder_1_out14), .out15(decoder_1_out15),
    .sel(counter_1_q), .en(1'b1));
  Transistor transistor_1 ();  // open: in, out, gate
  Pull_Resistor pull_resistor_1 (.node(wash));
  Transistor transistor_2 (.in(decoder_1_out0), .out(wash), .gate(in_1));
  Transistor transistor_3 (.in(decoder_1_out1), .out(wash), .gate(in_1));
  Transistor transistor_4 (.in(decoder_1_out2), .out(wash), .gate(in_1));
  Transistor transistor_5 (.in(decoder_1_out3), .out(wash), .gate(in_1));
  Transistor transistor_6 (.in(decoder_1_out4), .out(wash), .gate(in_1));
  Pull_Resistor pull_resistor_2 (.node(rinse));
  Transistor transistor_7 (.in(decoder_1_out5), .out(rinse), .gate(in_1));
  Transistor transistor_8 (.in(decoder_1_out6), .out(rinse), .gate(in_1));
  Transistor transistor_9 (.in(decoder_1_out7), .out(rinse), .gate(in_1));
  Transistor transistor_10 (.in(decoder_1_out8), .out(rinse), .gate(in_1));
  Pull_Resistor pull_resistor_3 (.node(spin));
  Transistor transistor_11 (.in(decoder_1_out9), .out(spin), .gate(in_1));
  Transistor transistor_12 (.in(decoder_1_out10), .out(spin), .gate(in_1));
  Transistor transistor_13 (.in(decoder_1_out11), .out(spin), .gate(in_1));
  Transistor transistor_14 (.in(decoder_1_out12), .out(spin), .gate(in_1));
  Pull_Resistor pull_resistor_4 (.node(stop));
  Transistor transistor_15 (.in(decoder_1_out13), .out(stop), .gate(in_1));
  Transistor transistor_16 (.in(decoder_1_out14), .out(stop), .gate(in_1));
  Transistor transistor_17 (.in(decoder_1_out15), .out(stop), .gate(in_1));
endmodule
